# Fritzing sketch breadboard_rat_v21 (saved by Fritzing 0.9.0b)
breadboards: 3

parts:
  MCP4922 = IC, DIP package, 14 pins [chip_label=MCP4922]
  Teensy1 = Teensy 3.0
  U2 = V_REG_LD1117VXX [package=78xxl]
  MCP4923 = IC, DIP package, 14 pins [chip_label=MCP4922]  # not connected
  MCP4924 = IC, DIP package, 14 pins [chip_label=MCP4922]  # not connected
  MCP4925 = IC, DIP package, 14 pins [chip_label=MCP4922]  # not connected
  MCP4926 = IC, DIP package, 14 pins [chip_label=MCP4922]  # not connected
  MCP4928 = IC, DIP package, 14 pins [chip_label=MCP4922]  # not connected
  MCP4929 = IC, DIP package, 14 pins [chip_label=MCP4922]
  C1 = Tantalum Capacitor [capacitance=1μF package="100 mil [THT, tantalum]"]
  C2 = Ceramic Capacitor [capacitance=100nF voltage=50V package="100 mil [THT, multilayer]"]
  MCP4930 = IC, DIP package, 14 pins [chip_label=MCP4922]  # not connected
  R13 = Resistor [tolerance=±5% resistance=220 package=THT]
  R14 = Resistor [tolerance=±5% resistance=220 package=THT]
  C3 = Ceramic Capacitor [capacitance=100nF package="100 mil [THT, multilayer]"]  # not connected

nets:
  N1: MCP4922.pin11, MCP4922.pin13
  N2: MCP4922.pin12, Teensy1.AGND
  GND: Teensy1.GND, U2.GND, C1.-, C2.0
  N3: Teensy1.Vin, U2.IN, C2.1
  N4: U2.OUT, C1.+
  N5: MCP4929.pin1, MCP4929.pin11, MCP4929.pin13
  N6: MCP4929.pin8, MCP4929.pin12, R13.Pin_1
  N7: MCP4929.pin14, R14.Pin_1
  N8: R13.Pin_0, R14.Pin_0
